// Logisim project ex3.circ as structural Verilog: 1 circuit, main circuit SplitThing
module SplitThing (
  input  [7:0] INPUT0,
  output OUTPUT0,
  output [7:0] OUTPUT1
);

  and and_1 (OUTPUT0, INPUT0[0], INPUT0[7]);

  assign OUTPUT1 = INPUT0;
endmodule
