// Logisim project ex5.circ as structural Verilog: 8 circuits, main circuit main
module main (
  input  D0,
  input  D1,
  input  D2,
  input  D3
);

  wire At, Bt, Ct, Dt, Et, Ft, Gt;

  SA sa_1 (.D0(D0), .D1(D1), .D2(D2), .D3(D3), .SA_out(At));
  SB sb_1 (.D0(D0), .D1(D1), .D2(D2), .D3(D3), .SB_out(Bt));
  SC sc_1 (.D0(D0), .D1(D1), .D2(D2), .D3(D3), .SC_out(Ct));
  SD sd_1 (.D0(D0), .D1(D1), .D2(D2), .D3(D3), .SD_out(Dt));
  SE se_1 (.D0(D0), .D1(D1), .D2(D2), .D3(D3), .SE_out(Et));
  SF sf_1 (.D0(D0), .D1(D1), .D2(D2), .D3(D3), .SF_out(Ft));
  SG sg_1 (.D0(D0), .D1(D1), .D2(D2), .D3(D3), .SA_out(Gt));
  LED led_1 (.in(At));
  LED led_2 (.in(At));
  LED led_3 (.in(Ft));
  LED led_4 (.in(Ft));
  LED led_5 (.in(Ft));
  LED led_6 (.in(Gt));
  LED led_7 (.in(Gt));
  LED led_8 (.in(Et));
  LED led_9 (.in(Et));
  LED led_10 (.in(Et));
  LED led_11 (.in(Dt));
  LED led_12 (.in(Dt));
  LED led_13 (.in(At));
  LED led_14 (.in(Bt));
  LED led_15 (.in(Bt));
  LED led_16 (.in(Bt));
  LED led_17 (.in(Gt));
  LED led_18 (.in(Ct));
  LED led_19 (.in(Ct));
  LED led_20 (.in(Ct));
  LED led_21 (.in(Dt));
endmodule

module SA (
  input  D0,
  input  D1,
  input  D2,
  input  D3,
  output SA_out
);

  wire and_1_out, and_2_out, and_3_out, and_4_out, not_1_out, not_2_out, not_3_out, not_4_out, not_5_out,
       not_6_out, not_7_out;

  not not_1 (not_1_out, D3);
  not not_2 (not_2_out, D3);
  not not_3 (not_3_out, D2);
  not not_4 (not_4_out, D1);
  not not_5 (not_5_out, D2);
  not not_6 (not_6_out, D1);
  not not_7 (not_7_out, D0);
  and and_1 (and_1_out, not_1_out, D1);
  and and_2 (and_2_out, not_2_out, D2, D0);
  and and_3 (and_3_out, D3, not_3_out, not_4_out);
  and and_4 (and_4_out, not_5_out, not_6_out, not_7_out);
  or or_1 (SA_out, and_1_out, and_2_out, and_3_out, and_4_out);
endmodule

module SB (
  input  D0,
  input  D1,
  input  D2,
  input  D3,
  output SB_out
);

  wire and_1_out, and_2_out, and_3_out, and_4_out, not_1_out, not_2_out, not_3_out, not_4_out, not_5_out,
       not_6_out, not_7_out, not_8_out;

  not not_1 (not_1_out, D3);
  not not_2 (not_2_out, D2);
  not not_3 (not_3_out, D2);
  not not_4 (not_4_out, D1);
  not not_5 (not_5_out, D3);
  not not_6 (not_6_out, D3);
  not not_7 (not_7_out, D1);
  not not_8 (not_8_out, D0);
  and and_1 (and_1_out, not_1_out, not_2_out);
  and and_2 (and_2_out, not_3_out, not_4_out);
  and and_3 (and_3_out, not_5_out, D1, D0);
  and and_4 (and_4_out, not_6_out, not_7_out, not_8_out);
  or or_1 (SB_out, and_1_out, and_2_out, and_3_out, and_4_out);
endmodule

module SC (
  input  D0,
  input  D1,
  input  D2,
  input  D3,
  output SC_out
);

  wire and_1_out, and_2_out, and_3_out, and_4_out, not_1_out, not_2_out, not_3_out, not_4_out, not_5_out,
       not_6_out;

  not not_1 (not_1_out, D3);
  not not_2 (not_2_out, D1);
  not not_3 (not_3_out, D2);
  not not_4 (not_4_out, D1);
  not not_5 (not_5_out, D3);
  not not_6 (not_6_out, D3);
  and and_1 (and_1_out, not_1_out, not_2_out);
  and and_2 (and_2_out, not_3_out, not_4_out);
  and and_3 (and_3_out, not_5_out, D2);
  and and_4 (and_4_out, not_6_out, D1, D0);
  or or_1 (SC_out, and_1_out, and_2_out, and_3_out, and_4_out);
endmodule

module SD (
  input  D0,
  input  D1,
  input  D2,
  input  D3,
  output SD_out
);

  wire and_1_out, and_2_out, and_3_out, and_4_out, and_5_out, not_1_out, not_2_out, not_3_out, not_4_out,
       not_5_out, not_6_out, not_7_out, not_8_out, not_9_out, not_10_out, not_11_out, not_12_out;

  not not_1 (not_1_out, D3);
  not not_2 (not_2_out, D2);
  not not_3 (not_3_out, D0);
  not not_4 (not_4_out, D3);
  not not_5 (not_5_out, D2);
  not not_6 (not_6_out, D3);
  not not_7 (not_7_out, D0);
  not not_8 (not_8_out, D2);
  not not_9 (not_9_out, D1);
  not not_10 (not_10_out, D0);
  not not_11 (not_11_out, D3);
  not not_12 (not_12_out, D1);
  and and_1 (and_1_out, not_1_out, not_2_out, not_3_out);
  and and_2 (and_2_out, not_4_out, not_5_out, D1);
  and and_3 (and_3_out, not_6_out, D1, not_7_out);
  and and_4 (and_4_out, not_8_out, not_9_out, not_10_out);
  and and_5 (and_5_out, not_11_out, D2, not_12_out, D0);
  or or_1 (SD_out, and_1_out, and_2_out, and_3_out, and_4_out, and_5_out);
endmodule

module SE (
  input  D0,
  input  D1,
  input  D2,
  input  D3,
  output SE_out
);

  wire and_1_out, and_2_out, and_3_out, not_1_out, not_2_out, not_3_out, not_4_out, not_5_out, not_6_out,
       not_7_out, not_8_out;

  not not_1 (not_1_out, D2);
  not not_2 (not_2_out, D1);
  not not_3 (not_3_out, D0);
  not not_4 (not_4_out, D3);
  not not_5 (not_5_out, D2);
  not not_6 (not_6_out, D0);
  not not_7 (not_7_out, D3);
  not not_8 (not_8_out, D0);
  and and_1 (and_1_out, not_1_out, not_2_out, not_3_out);
  and and_2 (and_2_out, not_4_out, not_5_out, not_6_out);
  and and_3 (and_3_out, not_7_out, D1, not_8_out);
  or or_1 (SE_out, and_1_out, and_2_out, and_3_out);
endmodule

module SF (
  input  D0,
  input  D1,
  input  D2,
  input  D3,
  output SF_out
);

  wire and_1_out, and_2_out, and_3_out, and_4_out, and_5_out, not_1_out, not_2_out, not_3_out, not_4_out,
       not_5_out, not_6_out, not_7_out, not_8_out, not_9_out, not_10_out, not_11_out, not_12_out;

  not not_1 (not_1_out, D2);
  not not_2 (not_2_out, D1);
  not not_3 (not_3_out, D0);
  not not_4 (not_4_out, D3);
  not not_5 (not_5_out, D1);
  not not_6 (not_6_out, D0);
  not not_7 (not_7_out, D3);
  not not_8 (not_8_out, D1);
  not not_9 (not_9_out, D3);
  not not_10 (not_10_out, D0);
  not not_11 (not_11_out, D2);
  not not_12 (not_12_out, D1);
  and and_1 (and_1_out, not_4_out, not_5_out, not_6_out);
  and and_2 (and_2_out, not_7_out, D2, not_8_out);
  and and_3 (and_3_out, not_9_out, D2, not_10_out);
  and and_4 (and_4_out, D3, not_11_out, not_12_out);
  and and_5 (and_5_out, not_1_out, not_2_out, not_3_out);
  or or_1 (SF_out, and_5_out, and_1_out, and_2_out, and_3_out, and_4_out);
endmodule

module SG (
  input  D0,
  input  D1,
  input  D2,
  input  D3,
  output SA_out
);

  wire and_1_out, and_2_out, and_3_out, and_4_out, and_5_out, and_6_out, not_1_out, not_2_out, not_3_out,
       not_4_out, not_5_out, not_6_out, not_7_out, not_8_out, not_9_out, not_10_out, not_11_out, not_12_out;

  not not_1 (not_1_out, D3);
  not not_2 (not_2_out, D2);
  not not_3 (not_3_out, D3);
  not not_4 (not_4_out, D0);
  not not_5 (not_5_out, D3);
  not not_6 (not_6_out, D0);
  not not_7 (not_7_out, D3);
  not not_8 (not_8_out, D1);
  not not_9 (not_9_out, D2);
  not not_10 (not_10_out, D1);
  not not_11 (not_11_out, D0);
  not not_12 (not_12_out, D2);
  and and_1 (and_1_out, not_1_out, not_2_out, D1);
  and and_2 (and_2_out, not_3_out, D1, not_4_out);
  and and_3 (and_3_out, not_5_out, D2, not_6_out);
  and and_4 (and_4_out, not_7_out, D2, not_8_out);
  and and_5 (and_5_out, D3, not_9_out, not_10_out);
  and and_6 (and_6_out, not_11_out, not_12_out, D3);
  or or_1 (SA_out, and_1_out, and_2_out, and_3_out, and_4_out, and_5_out, and_6_out);
endmodule
